// Logisim project 4_bitmicrocontroller.circ as structural Verilog
module half_adder (
  input  A,
  input  B,
  output sum,
  output carry
);

  xor xor_1 (sum, A, B);
  and and_1 (carry, A, B);
endmodule

module full_adder (
  input  A,
  input  B,
  input  CIn,
  output SUM,
  output Cout
);

  wire half_adder_1_carry, half_adder_1_sum, half_adder_2_carry;

  half_adder half_adder_1 (.A(A), .B(B), .sum(half_adder_1_sum), .carry(half_adder_1_carry));
  half_adder half_adder_2 (.A(half_adder_1_sum), .B(CIn), .sum(SUM), .carry(half_adder_2_carry));
  or or_1 (Cout, half_adder_1_carry, half_adder_2_carry);
endmodule

module _4_bit_adder (
  input  A0,
  input  A1,
  input  A2,
  input  A3,
  input  B0,
  input  B1,
  input  B2,
  input  B3,
  output S0,
  output S1,
  output S2,
  output S3,
  output COUT
);

  wire full_adder_1_cout, full_adder_2_cout, half_adder_1_carry;

  half_adder half_adder_1 (.A(A0), .B(B0), .sum(S0), .carry(half_adder_1_carry));
  full_adder full_adder_1 (.A(A1), .B(B1), .CIn(half_adder_1_carry), .SUM(S1), .Cout(full_adder_1_cout));
  full_adder full_adder_2 (.A(A2), .B(B2), .CIn(full_adder_1_cout), .SUM(S2), .Cout(full_adder_2_cout));
  full_adder full_adder_3 (.A(A3), .B(B3), .CIn(full_adder_2_cout), .SUM(S3), .Cout(COUT));
endmodule

module ADDER_SUBTRATOR (
  input  A0,
  input  A1,
  input  A2,
  input  A3,
  input  B0,
  input  B1,
  input  B2,
  input  B3,
  input  CTR,
  output S0,
  output S1,
  output S2,
  output S3,
  output out_14
);

  wire n4_bit_adder_1_s0, n4_bit_adder_1_s1, n4_bit_adder_1_s2, n4_bit_adder_1_s3, xor_1_out, xor_2_out,
       xor_3_out, xor_4_out;

  xor xor_1 (xor_1_out, CTR, B0);
  xor xor_2 (xor_2_out, CTR, B1);
  xor xor_3 (xor_3_out, CTR, B2);
  xor xor_4 (xor_4_out, CTR, B3);
  _4_bit_adder u_4_bit_adder_1 (
    .A0(xor_1_out), .A1(xor_2_out), .A2(xor_3_out), .A3(xor_4_out), .B0(CTR), .B1(1'b0), .B2(1'b0),
    .B3(1'b0), .S0(n4_bit_adder_1_s0), .S1(n4_bit_adder_1_s1), .S2(n4_bit_adder_1_s2), .S3(n4_bit_adder_1_s3));  // open: COUT
  _4_BIT_ADDER_2_0 u_4_bit_adder_2_0_1 (
    .A0(A0), .A1(A1), .A2(A2), .A3(A3), .B0(n4_bit_adder_1_s0), .B1(n4_bit_adder_1_s1),
    .B2(n4_bit_adder_1_s2), .B3(n4_bit_adder_1_s3), .S0(S0), .S2(S1), .S2_2(S2), .S3(S3), .COUT(out_14));  // open: CX
endmodule

module multiplier (
  input  B0,
  input  A0,
  input  A1,
  input  A2,
  input  A3,
  input  B1,
  input  B2,
  input  B3,
  output P0,
  output P1,
  output P2,
  output P3,
  output P4,
  output P5,
  output P6,
  output P7
);

  wire and_2_out, and_3_out, and_4_out, and_5_out, and_6_out, and_7_out, and_8_out, and_9_out, and_10_out,
       and_11_out, and_12_out, and_13_out, and_14_out, and_15_out, and_16_out, n4_bit_adder_1_cout,
       n4_bit_adder_1_s1, n4_bit_adder_1_s2, n4_bit_adder_1_s3, n4_bit_adder_2_cout, n4_bit_adder_2_s1,
       n4_bit_adder_2_s2, n4_bit_adder_2_s3;

  and and_1 (P0, B0, B0, A0);
  and and_2 (and_2_out, B0, A1);
  and and_3 (and_3_out, B0, A2);
  and and_4 (and_4_out, B0, A3);
  and and_5 (and_5_out, B1, A0);
  and and_6 (and_6_out, A1, B1);
  and and_7 (and_7_out, A2, B1);
  and and_8 (and_8_out, B1, A3);
  _4_bit_adder u_4_bit_adder_1 (
    .A0(and_2_out), .A1(and_3_out), .A2(and_4_out), .A3(1'b0), .B0(and_5_out), .B1(and_6_out),
    .B2(and_7_out), .B3(and_8_out), .S0(P1), .S1(n4_bit_adder_1_s1), .S2(n4_bit_adder_1_s2),
    .S3(n4_bit_adder_1_s3), .COUT(n4_bit_adder_1_cout));
  and and_9 (and_9_out, B2, A0);
  and and_10 (and_10_out, B2, A1);
  and and_11 (and_11_out, B2, A2);
  and and_12 (and_12_out, B2, A3);
  _4_bit_adder u_4_bit_adder_2 (
    .A0(n4_bit_adder_1_s1), .A1(n4_bit_adder_1_s2), .A2(n4_bit_adder_1_s3), .A3(n4_bit_adder_1_cout),
    .B0(and_9_out), .B1(and_10_out), .B2(and_11_out), .B3(and_12_out), .S0(P2), .S1(n4_bit_adder_2_s1),
    .S2(n4_bit_adder_2_s2), .S3(n4_bit_adder_2_s3), .COUT(n4_bit_adder_2_cout));
  and and_13 (and_13_out, B3, A0);
  and and_14 (and_14_out, B3, A1);
  and and_15 (and_15_out, B3, A2);
  and and_16 (and_16_out, B3, A3);
  _4_bit_adder u_4_bit_adder_3 (
    .A0(n4_bit_adder_2_s1), .A1(n4_bit_adder_2_s2), .A2(n4_bit_adder_2_s3), .A3(n4_bit_adder_2_cout),
    .B0(and_13_out), .B1(and_14_out), .B2(and_15_out), .B3(and_16_out), .S0(P3), .S1(P4), .S2(P5), .S3(P6),
    .COUT(P7));
endmodule

module _4_BIT_ADDER_2_0 (
  input  A0,
  input  A1,
  input  A2,
  input  A3,
  input  B0,
  input  B1,
  input  B2,
  input  B3,
  output S0,
  output S2,
  output S2_2,
  output S3,
  output COUT,
  output CX
);

  wire full_adder_1_cout, half_adder_1_carry;

  half_adder half_adder_1 (.A(A0), .B(B0), .sum(S0), .carry(half_adder_1_carry));
  full_adder full_adder_1 (.A(A1), .B(B1), .CIn(half_adder_1_carry), .SUM(S2), .Cout(full_adder_1_cout));
  full_adder full_adder_2 (.A(A2), .B(B2), .CIn(full_adder_1_cout), .SUM(S2_2), .Cout(CX));
  full_adder full_adder_3 (.A(A3), .B(B3), .CIn(CX), .SUM(S3), .Cout(COUT));
endmodule

module ALU (
  input  A0,
  input  A1,
  input  A2,
  input  A3,
  input  B0,
  input  B1,
  input  B2,
  input  B3,
  input  E,
  input  SEL,
  input  CTR,
  output P0,
  output P1,
  output P2,
  output P3,
  output P4,
  output P5,
  output P6,
  output P7,
  output S0,
  output S1,
  output S2,
  output S3,
  output COUT
);

  wire demultiplexer_1_out0, demultiplexer_1_out1, demultiplexer_2_out0, demultiplexer_2_out1,
       demultiplexer_3_out0, demultiplexer_3_out1, demultiplexer_4_out0, demultiplexer_4_out1,
       demultiplexer_5_out0, demultiplexer_5_out1, demultiplexer_6_out0, demultiplexer_6_out1,
       demultiplexer_7_out0, demultiplexer_7_out1, demultiplexer_8_out0, demultiplexer_8_out1;

  Demultiplexer demultiplexer_1 (.out0(demultiplexer_1_out0), .out1(demultiplexer_1_out1), .in(A0), .sel(SEL), .en(E));
  Demultiplexer demultiplexer_2 (.out0(demultiplexer_2_out0), .out1(demultiplexer_2_out1), .in(A1), .sel(SEL), .en(E));
  Demultiplexer demultiplexer_3 (.out0(demultiplexer_3_out0), .out1(demultiplexer_3_out1), .in(A2), .sel(SEL), .en(E));
  Demultiplexer demultiplexer_4 (.out0(demultiplexer_4_out0), .out1(demultiplexer_4_out1), .in(A3), .sel(SEL), .en(E));
  Demultiplexer demultiplexer_5 (.out0(demultiplexer_5_out0), .out1(demultiplexer_5_out1), .in(B0), .sel(SEL), .en(E));
  Demultiplexer demultiplexer_6 (.out0(demultiplexer_6_out0), .out1(demultiplexer_6_out1), .in(B1), .sel(SEL), .en(E));
  Demultiplexer demultiplexer_7 (.out0(demultiplexer_7_out0), .out1(demultiplexer_7_out1), .in(B2), .sel(SEL), .en(E));
  Demultiplexer demultiplexer_8 (.out0(demultiplexer_8_out0), .out1(demultiplexer_8_out1), .in(B3), .sel(SEL), .en(E));
  ADDER_SUBTRATOR adder_subtrator_1 (
    .A0(demultiplexer_1_out1), .A1(demultiplexer_2_out1), .A2(demultiplexer_3_out1),
    .A3(demultiplexer_4_out1), .B0(demultiplexer_5_out1), .B1(demultiplexer_6_out1),
    .B2(demultiplexer_7_out1), .B3(demultiplexer_8_out1), .CTR(CTR), .S0(S0), .S1(S1), .S2(S2), .S3(S3),
    .out_14(COUT));
  multiplier multiplier_1 (
    .B0(demultiplexer_5_out0), .A0(demultiplexer_1_out0), .A1(demultiplexer_2_out0),
    .A2(demultiplexer_3_out0), .A3(demultiplexer_4_out0), .B1(demultiplexer_6_out0),
    .B2(demultiplexer_7_out0), .B3(demultiplexer_8_out0), .P0(P0), .P1(P1), .P2(P2), .P3(P3), .P4(P4),
    .P5(P5), .P6(P6), .P7(P7));

  // Notes on the sheet:
  //   ADD/SUB
  //   PRODUCT
endmodule
