// Logisim project 7segDecoding EPROM version 1.circ as structural Verilog: 1 circuit, main circuit main
module main (
  input  [3:0] in_1,
  output g1,
  output f1,
  output e1,
  output d1,
  output c1,
  output b1,
  output a1,
  output g2,
  output f2,
  output e2,
  output d2,
  output c2,
  output b2,
  output a2
);

  wire [15:7] rom_1_data;

  ROM #(.addrWidth(4), .dataWidth(16)) rom_1 (
    .addr(in_1),
    .data({rom_1_data[15], a2, b2, c2, d2, e2, f2, g2, rom_1_data[7], a1, b1, c1, d1, e1, f1, g1}));  // open: sel

  // Notes on the sheet:
  //   contents of rom_1 (hex, n*v repeats v):
  //   7e7e 7e30 7e6d 7e79 7e33 7e5b 7e5f 7e70 7eff 7e7b 307e 3030 306d 3079 3033 305b
endmodule
