// Logisim project ALU.circ as structural Verilog
module half_adder (
  input  A,
  input  B,
  output sum,
  output carry
);

  xor xor_1 (sum, A, B);
  and and_1 (carry, A, B);
endmodule

module full_adder (
  input  A,
  input  B,
  input  CIn,
  output SUM,
  output Cout
);

  wire half_adder_1_carry, half_adder_1_sum, half_adder_2_carry;

  half_adder half_adder_1 (.A(A), .B(B), .sum(half_adder_1_sum), .carry(half_adder_1_carry));
  half_adder half_adder_2 (.A(half_adder_1_sum), .B(CIn), .sum(SUM), .carry(half_adder_2_carry));
  or or_1 (Cout, half_adder_1_carry, half_adder_2_carry);
endmodule

module _4_bit_adder (
  input  A0,
  input  A1,
  input  A2,
  input  A3,
  input  B0,
  input  B1,
  input  B2,
  input  B3,
  output S0,
  output S1,
  output S2,
  output S3,
  output COUT
);

  wire full_adder_1_cout, full_adder_2_cout, half_adder_1_carry;

  half_adder half_adder_1 (.A(A0), .B(B0), .sum(S0), .carry(half_adder_1_carry));
  full_adder full_adder_1 (.A(A1), .B(B1), .CIn(half_adder_1_carry), .SUM(S1), .Cout(full_adder_1_cout));
  full_adder full_adder_2 (.A(A2), .B(B2), .CIn(full_adder_1_cout), .SUM(S2), .Cout(full_adder_2_cout));
  full_adder full_adder_3 (.A(A3), .B(B3), .CIn(full_adder_2_cout), .SUM(S3), .Cout(COUT));
endmodule

module ADDER_SUBTRATOR (
  input  A0,
  input  A1,
  input  A2,
  input  A3,
  input  B0,
  input  B1,
  input  B2,
  input  B3,
  input  CTR,
  output S0,
  output S1,
  output S2,
  output S3,
  output sign,
  output zero,
  output carry,
  output overflow,
  output Negative
);

  wire n4_bit_adder_1_s0, n4_bit_adder_1_s1, n4_bit_adder_1_s2, n4_bit_adder_1_s3, n4_bit_adder_2_0_1_cx,
       not_1_out, not_2_out, not_3_out, not_4_out, not_5_out, xnor_1_out, xor_1_out, xor_2_out, xor_3_out,
       xor_4_out;

  xor xor_1 (xor_1_out, CTR, B0);
  xor xor_2 (xor_2_out, CTR, B1);
  xor xor_3 (xor_3_out, CTR, B2);
  xor xor_4 (xor_4_out, CTR, B3);
  _4_bit_adder u_4_bit_adder_1 (
    .A0(xor_1_out), .A1(xor_2_out), .A2(xor_3_out), .A3(xor_4_out), .B0(CTR), .B1(1'b0), .B2(1'b0),
    .B3(1'b0), .S0(n4_bit_adder_1_s0), .S1(n4_bit_adder_1_s1), .S2(n4_bit_adder_1_s2), .S3(n4_bit_adder_1_s3));  // open: COUT
  _4_BIT_ADDER_2_0 u_4_bit_adder_2_0_1 (
    .A0(A0), .A1(A1), .A2(A2), .A3(A3), .B0(n4_bit_adder_1_s0), .B1(n4_bit_adder_1_s1),
    .B2(n4_bit_adder_1_s2), .B3(n4_bit_adder_1_s3), .S0(S0), .S2(S1), .S2_2(S2), .S3(S3), .COUT(carry),
    .CX(n4_bit_adder_2_0_1_cx));
  xnor xnor_1 (xnor_1_out, A3, n4_bit_adder_1_s3);
  and and_1 (overflow, n4_bit_adder_2_0_1_cx, xnor_1_out);
  not not_1 (not_1_out, carry);
  and and_2 (Negative, not_1_out, CTR);
  not not_2 (not_2_out, S0);
  not not_3 (not_3_out, S1);
  not not_4 (not_4_out, S2);
  not not_5 (not_5_out, S3);
  ExactlyOne xor_5 (.out(sign), .in1(S3), .in2(overflow), .in3(overflow), .in4(overflow));
  and and_3 (zero, not_2_out, not_3_out, not_4_out, not_5_out);
endmodule

module multiplier (
  input  B0,
  input  A0,
  input  A1,
  input  A2,
  input  A3,
  input  B1,
  input  B2,
  input  B3,
  output P0,
  output P1,
  output P2,
  output P3,
  output P4,
  output P5,
  output P6,
  output P7
);

  wire and_2_out, and_3_out, and_4_out, and_5_out, and_6_out, and_7_out, and_8_out, and_9_out, and_10_out,
       and_11_out, and_12_out, and_13_out, and_14_out, and_15_out, and_16_out, n4_bit_adder_1_cout,
       n4_bit_adder_1_s1, n4_bit_adder_1_s2, n4_bit_adder_1_s3, n4_bit_adder_2_cout, n4_bit_adder_2_s1,
       n4_bit_adder_2_s2, n4_bit_adder_2_s3;

  and and_1 (P0, B0, B0, A0);
  and and_2 (and_2_out, B0, A1);
  and and_3 (and_3_out, B0, A2);
  and and_4 (and_4_out, B0, A3);
  and and_5 (and_5_out, B1, A0);
  and and_6 (and_6_out, A1, B1);
  and and_7 (and_7_out, A2, B1);
  and and_8 (and_8_out, B1, A3);
  _4_bit_adder u_4_bit_adder_1 (
    .A0(and_2_out), .A1(and_3_out), .A2(and_4_out), .A3(1'b0), .B0(and_5_out), .B1(and_6_out),
    .B2(and_7_out), .B3(and_8_out), .S0(P1), .S1(n4_bit_adder_1_s1), .S2(n4_bit_adder_1_s2),
    .S3(n4_bit_adder_1_s3), .COUT(n4_bit_adder_1_cout));
  and and_9 (and_9_out, B2, A0);
  and and_10 (and_10_out, B2, A1);
  and and_11 (and_11_out, B2, A2);
  and and_12 (and_12_out, B2, A3);
  _4_bit_adder u_4_bit_adder_2 (
    .A0(n4_bit_adder_1_s1), .A1(n4_bit_adder_1_s2), .A2(n4_bit_adder_1_s3), .A3(n4_bit_adder_1_cout),
    .B0(and_9_out), .B1(and_10_out), .B2(and_11_out), .B3(and_12_out), .S0(P2), .S1(n4_bit_adder_2_s1),
    .S2(n4_bit_adder_2_s2), .S3(n4_bit_adder_2_s3), .COUT(n4_bit_adder_2_cout));
  and and_13 (and_13_out, B3, A0);
  and and_14 (and_14_out, B3, A1);
  and and_15 (and_15_out, B3, A2);
  and and_16 (and_16_out, B3, A3);
  _4_bit_adder u_4_bit_adder_3 (
    .A0(n4_bit_adder_2_s1), .A1(n4_bit_adder_2_s2), .A2(n4_bit_adder_2_s3), .A3(n4_bit_adder_2_cout),
    .B0(and_13_out), .B1(and_14_out), .B2(and_15_out), .B3(and_16_out), .S0(P3), .S1(P4), .S2(P5), .S3(P6),
    .COUT(P7));
endmodule

module _4_BIT_ADDER_2_0 (
  input  A0,
  input  A1,
  input  A2,
  input  A3,
  input  B0,
  input  B1,
  input  B2,
  input  B3,
  output S0,
  output S2,
  output S2_2,
  output S3,
  output COUT,
  output CX
);

  wire full_adder_1_cout, half_adder_1_carry;

  half_adder half_adder_1 (.A(A0), .B(B0), .sum(S0), .carry(half_adder_1_carry));
  full_adder full_adder_1 (.A(A1), .B(B1), .CIn(half_adder_1_carry), .SUM(S2), .Cout(full_adder_1_cout));
  full_adder full_adder_2 (.A(A2), .B(B2), .CIn(full_adder_1_cout), .SUM(S2_2), .Cout(CX));
  full_adder full_adder_3 (.A(A3), .B(B3), .CIn(CX), .SUM(S3), .Cout(COUT));
endmodule

module ALU (
  input  Ain,
  input  A0,
  input  A1,
  input  A2,
  input  in_5,
  input  BIN,
  input  B0,
  input  B1,
  input  B2,
  input  B3,
  input  E,
  input  SEL,
  input  CTR,
  output P0,
  output P1,
  output P2,
  output P3,
  output P4,
  output P5,
  output P6,
  output P7,
  output ZERO,
  output S0,
  output S1,
  output S2,
  output S3,
  output SIGN,
  output CARRY,
  output OVERFLOW,
  output NEGATIVE
);

  wire adder_subtrator_1_sign, adder_subtrator_1_zero, and_1_out, demultiplexer_1_out0, demultiplexer_1_out1,
       demultiplexer_2_out0, demultiplexer_2_out1, demultiplexer_3_out0, demultiplexer_3_out1,
       demultiplexer_4_out0, demultiplexer_4_out1, demultiplexer_5_out0, demultiplexer_6_out0,
       demultiplexer_6_out1, demultiplexer_7_out0, demultiplexer_7_out1, demultiplexer_8_out0,
       demultiplexer_8_out1, not_1_out, not_2_out, not_3_out, not_4_out, not_5_out, not_6_out, not_7_out,
       not_8_out, parllel_loading_to_register_1_r0, parllel_loading_to_register_1_r1,
       parllel_loading_to_register_1_r2, parllel_loading_to_register_1_r3, parllel_loading_to_register_2_r0,
       parllel_loading_to_register_2_r1, parllel_loading_to_register_2_r2, parllel_loading_to_register_2_r3;

  PARLLEL_LOADING_TO_REGISTER parllel_loading_to_register_1 (
    .CONTROL(Ain), .D0(A0), .D1(A1), .D2(A2), .D3(in_5), .R0(parllel_loading_to_register_1_r0),
    .R1(parllel_loading_to_register_1_r1), .R2(parllel_loading_to_register_1_r2),
    .R3(parllel_loading_to_register_1_r3));
  PARLLEL_LOADING_TO_REGISTER parllel_loading_to_register_2 (
    .CONTROL(BIN), .D0(B0), .D1(B1), .D2(B2), .D3(B3), .R0(parllel_loading_to_register_2_r0),
    .R1(parllel_loading_to_register_2_r1), .R2(parllel_loading_to_register_2_r2),
    .R3(parllel_loading_to_register_2_r3));
  Demultiplexer demultiplexer_1 (
    .out0(demultiplexer_1_out0), .out1(demultiplexer_1_out1), .in(parllel_loading_to_register_1_r0),
    .sel(SEL), .en(E));
  Demultiplexer demultiplexer_2 (
    .out0(demultiplexer_2_out0), .out1(demultiplexer_2_out1), .in(parllel_loading_to_register_1_r1),
    .sel(SEL), .en(E));
  Demultiplexer demultiplexer_3 (
    .out0(demultiplexer_3_out0), .out1(demultiplexer_3_out1), .in(parllel_loading_to_register_1_r2),
    .sel(SEL), .en(E));
  Demultiplexer demultiplexer_4 (
    .out0(demultiplexer_4_out0), .out1(demultiplexer_4_out1), .in(parllel_loading_to_register_1_r3),
    .sel(SEL), .en(E));
  Demultiplexer demultiplexer_5 (
    .out0(demultiplexer_5_out0), .out1(demultiplexer_4_out1), .in(parllel_loading_to_register_2_r0),
    .sel(SEL), .en(E));
  Demultiplexer demultiplexer_6 (
    .out0(demultiplexer_6_out0), .out1(demultiplexer_6_out1), .in(parllel_loading_to_register_2_r1),
    .sel(SEL), .en(E));
  Demultiplexer demultiplexer_7 (
    .out0(demultiplexer_7_out0), .out1(demultiplexer_7_out1), .in(parllel_loading_to_register_2_r2),
    .sel(SEL), .en(E));
  Demultiplexer demultiplexer_8 (
    .out0(demultiplexer_8_out0), .out1(demultiplexer_8_out1), .in(parllel_loading_to_register_2_r3),
    .sel(SEL), .en(E));
  ADDER_SUBTRATOR adder_subtrator_1 (
    .A0(demultiplexer_1_out1), .A1(demultiplexer_2_out1), .A2(demultiplexer_3_out1),
    .A3(demultiplexer_4_out1), .B0(demultiplexer_4_out1), .B1(demultiplexer_6_out1),
    .B2(demultiplexer_7_out1), .B3(demultiplexer_8_out1), .CTR(CTR), .S0(S0), .S1(S1), .S2(S2), .S3(S3),
    .sign(adder_subtrator_1_sign), .zero(adder_subtrator_1_zero), .carry(CARRY), .overflow(OVERFLOW),
    .Negative(NEGATIVE));
  multiplier multiplier_1 (
    .B0(demultiplexer_5_out0), .A0(demultiplexer_1_out0), .A1(demultiplexer_2_out0),
    .A2(demultiplexer_3_out0), .A3(demultiplexer_4_out0), .B1(demultiplexer_6_out0),
    .B2(demultiplexer_7_out0), .B3(demultiplexer_8_out0), .P0(P0), .P1(P1), .P2(P2), .P3(P3), .P4(P4),
    .P5(P5), .P6(P6), .P7(P7));
  not not_1 (not_1_out, P0);
  not not_2 (not_2_out, P1);
  not not_3 (not_3_out, P2);
  not not_4 (not_4_out, P3);
  not not_5 (not_5_out, P4);
  not not_6 (not_6_out, P5);
  not not_7 (not_7_out, P6);
  not not_8 (not_8_out, P7);
  Multiplexer multiplexer_1 (.in0(and_1_out), .in1(adder_subtrator_1_zero), .out(ZERO), .sel(SEL), .en(1'b1));
  Multiplexer multiplexer_2 (.in0(P7), .in1(adder_subtrator_1_sign), .out(SIGN), .sel(SEL), .en(1'b1));
  and and_1 (and_1_out, not_1_out, not_2_out, not_3_out, not_4_out, not_5_out, not_6_out, not_7_out, not_8_out);

  // Notes on the sheet:
  //   0 FOR MULTIPLICATION
  //   1 FOR ADD AND SUBTRACT
  //   0 FOR ADD
  //   1 FOR SUBTRACT
  //   ADD/SUB
  //   PRODUCT
endmodule
