// Logisim project CPU version 1.circ as structural Verilog: 1 circuit, main circuit main
module main (
  input  A0,
  input  A1,
  input  A2,
  input  A3,
  input  A4,
  input  A5,
  input  A6,
  input  A7,
  input  JUMP_SIGNAL,
  input  COUNT_INCREMENT,
  input  PC_OUT,
  input  CLK,
  input  VCC
);

  wire [7:0] controlled_buffer_1_out, counter_1_q;
  wire [15:0] register_1_q, rom_1_data, rom_2_data;

  ROM #(.dataWidth(16)) rom_1 (.addr(controlled_buffer_1_out), .data(rom_1_data), .sel(VCC));
  assign controlled_buffer_1_out = PC_OUT ? counter_1_q : 8'bz;  // Controlled_Buffer controlled_buffer_1
  Counter counter_1 (
    .load(JUMP_SIGNAL), .D({A7, A6, A5, A4, A3, A2, A1, A0}), .count(COUNT_INCREMENT), .Q(counter_1_q),
    .clk(CLK));  // open: carry, clr
  Register #(.width(16)) register_1 (.D(rom_1_data), .en(VCC), .Q(register_1_q), .clk(CLK));  // open: clr
  ROM #(.addrWidth(16), .dataWidth(16)) rom_2 (.addr(register_1_q), .data(rom_2_data), .sel(VCC));

  // Notes on the sheet:
  //   Flash ROM
  //   Instruction Register
  //   Program Counter
  //   EPROM
  //   CONTROL SIGNALS
  //   ADRESS FROM JUMP INSTRUCTION
endmodule
