// Logisim project DecoderRegisters.circ as structural Verilog: 1 circuit, main circuit main
module main (
);

  wire and_1_out, and_2_out, and_3_out, and_4_out, and_5_out, and_6_out, and_7_out, and_8_out, and_9_out,
       and_10_out, and_11_out, and_12_out, and_13_out, and_14_out, and_15_out, and_16_out, decoder_1_out0,
       decoder_1_out1, decoder_1_out2, decoder_1_out3, decoder_1_out4, decoder_1_out5, decoder_1_out6,
       decoder_1_out7, nor_1_out, undriven, undriven_2, undriven_4, undriven_5, undriven_6, undriven_7;
  wire [2:0] undriven_3;
  wire [3:0] register_1_q, register_2_q, register_3_q, register_4_q, register_5_q, register_6_q,
       register_7_q, register_8_q;

  nor nor_1 (nor_1_out, undriven, undriven_2);
  Decoder #(.select(3)) decoder_1 (
    .out0(decoder_1_out0), .out1(decoder_1_out1), .out2(decoder_1_out2), .out3(decoder_1_out3),
    .out4(decoder_1_out4), .out5(decoder_1_out5), .out6(decoder_1_out6), .out7(decoder_1_out7),
    .sel(undriven_3), .en(nor_1_out));
  and and_1 (and_1_out, undriven_5, decoder_1_out0);
  and and_2 (and_2_out, decoder_1_out0, undriven_4);
  and and_3 (and_3_out, undriven_5, decoder_1_out2);
  and and_4 (and_4_out, decoder_1_out2, undriven_4);
  and and_5 (and_5_out, undriven_5, decoder_1_out4);
  and and_6 (and_6_out, decoder_1_out4, undriven_4);
  and and_7 (and_7_out, undriven_5, decoder_1_out6);
  and and_8 (and_8_out, decoder_1_out6, undriven_4);
  Register #(.width(4), .trigger("falling")) register_1 (
    .en(and_1_out), .clk(undriven_7), .Q(register_1_q), .clr(undriven_6));  // open: D
  Register #(.width(4), .trigger("falling")) register_2 (
    .en(and_3_out), .clk(undriven_7), .Q(register_2_q), .clr(undriven_6));  // open: D
  Register #(.width(4), .trigger("falling")) register_3 (
    .en(and_5_out), .clk(undriven_7), .Q(register_3_q), .clr(undriven_6));  // open: D
  Register #(.width(4), .trigger("falling")) register_4 (
    .en(and_7_out), .clk(undriven_7), .Q(register_4_q), .clr(undriven_6));  // open: D
  Controlled_Buffer #(.width(4)) controlled_buffer_1 (.in(register_1_q), .en(and_2_out));  // open: out
  Controlled_Buffer #(.width(4)) controlled_buffer_2 (.in(register_2_q), .en(and_4_out));  // open: out
  Controlled_Buffer #(.width(4)) controlled_buffer_3 (.in(register_3_q), .en(and_6_out));  // open: out
  Controlled_Buffer #(.width(4)) controlled_buffer_4 (.in(register_4_q), .en(and_8_out));  // open: out
  and and_9 (and_9_out, undriven_5, decoder_1_out1);
  and and_10 (and_10_out, decoder_1_out1, undriven_4);
  and and_11 (and_11_out, undriven_5, decoder_1_out3);
  and and_12 (and_12_out, decoder_1_out3, undriven_4);
  and and_13 (and_13_out, undriven_5, decoder_1_out5);
  and and_14 (and_14_out, decoder_1_out5, undriven_4);
  and and_15 (and_15_out, undriven_5, decoder_1_out7);
  and and_16 (and_16_out, decoder_1_out7, undriven_4);
  Register #(.width(4), .trigger("falling")) register_5 (
    .en(and_9_out), .clk(undriven_7), .Q(register_5_q), .clr(undriven_6));  // open: D
  Register #(.width(4), .trigger("falling")) register_6 (
    .en(and_11_out), .clk(undriven_7), .Q(register_6_q), .clr(undriven_6));  // open: D
  Register #(.width(4), .trigger("falling")) register_7 (
    .en(and_13_out), .clk(undriven_7), .Q(register_7_q), .clr(undriven_6));  // open: D
  Register #(.width(4), .trigger("falling")) register_8 (
    .en(and_15_out), .clk(undriven_7), .Q(register_8_q), .clr(undriven_6));  // open: D
  Controlled_Buffer #(.width(4)) controlled_buffer_5 (.in(register_5_q), .en(and_10_out));  // open: out
  Controlled_Buffer #(.width(4)) controlled_buffer_6 (.in(register_6_q), .en(and_12_out));  // open: out
  Controlled_Buffer #(.width(4)) controlled_buffer_7 (.in(register_7_q), .en(and_14_out));  // open: out
  Controlled_Buffer #(.width(4)) controlled_buffer_8 (.in(register_8_q), .en(and_16_out));  // open: out

  // Notes on the sheet:
  //   A4
  //   A3
  //   Address 3bits
  //   Rout
  //   Rin
  //   CLK
  //   reset
endmodule
