// Logisim project Harvard-Architecture-based-4-bit-processor.circ as structural Verilog: 1 circuit, main circuit main
module main (
  input  [7:0] Address_pins,
  input  [18:0] in_2
);

  wire clock_1_out, decoder_1_out0, decoder_1_out1, decoder_1_out2, decoder_1_out3, decoder_1_out4,
       decoder_1_out5, decoder_1_out6, decoder_1_out7, main_1_a1, main_1_a2, main_1_b1, main_1_b2, main_1_c1,
       main_1_c2, main_1_d1, main_1_d2, main_1_e1, main_1_e2, main_1_f1, main_1_f2, main_1_g1, main_1_g2,
       not_1_out, undriven;
  wire [1:0] main_4_p5, register_6_q;
  wire [2:0] counter_1_q;
  wire [3:0] main_4_p3, main_4_p4, register_2_q, register_4_q, register_5_q;
  wire [4:0] controlled_buffer_2_out, controlled_buffer_3_out, register_1_q_2;
  wire [7:0] controlled_buffer_1_out, counter_2_q;
  wire [15:0] register_1_q, rom_1_data;
  wire [18:0] rom_2_data;

  Clock clock_1 (.out(clock_1_out));
  not not_1 (not_1_out, clock_1_out);
  LED led_1 (.in(not_1_out));
  _7segDecoding_EPROM_version_1_main main_1 (
    .g1(main_1_g1), .f1(main_1_f1), .e1(main_1_e1), .d1(main_1_d1), .c1(main_1_c1), .b1(main_1_b1),
    .a1(main_1_a1), .g2(main_1_g2), .f2(main_1_f2), .e2(main_1_e2), .d2(main_1_d2), .c2(main_1_c2),
    .b2(main_1_b2), .a2(main_1_a2), .in_1(register_5_q));
  ROM #(.dataWidth(16)) rom_1 (.addr(controlled_buffer_1_out), .data(rom_1_data));  // open: sel
  Counter #(.width(3), .max('h7)) counter_1 (
    .count(1'b1), .Q(counter_1_q), .clk(not_1_out), .clr(rom_2_data[2]));  // open: load, D, carry
  Decoder #(.select(3)) decoder_1 (
    .out0(decoder_1_out0), .out1(decoder_1_out1), .out2(decoder_1_out2), .out3(decoder_1_out3),
    .out4(decoder_1_out4), .out5(decoder_1_out5), .out6(decoder_1_out6), .out7(decoder_1_out7),
    .sel(counter_1_q));  // open: en
  LED led_2 (.in(decoder_1_out0));
  LED led_3 (.in(decoder_1_out2));
  LED led_4 (.in(decoder_1_out1));
  _7_Segment_Display u_7_segment_display_1 (
    .g(main_1_g2), .f(main_1_f2), .a(main_1_b2), .b(main_1_a2), .e(main_1_e2), .d(main_1_d2), .c(main_1_c2));  // open: dp
  LED led_5 (.in(decoder_1_out5));
  LED led_6 (.in(decoder_1_out4));
  LED led_7 (.in(decoder_1_out6));
  LED led_8 (.in(decoder_1_out3));
  _7_Segment_Display u_7_segment_display_2 (
    .g(main_1_g1), .f(main_1_f1), .a(main_1_b1), .b(main_1_a1), .e(main_1_e1), .d(main_1_d1), .c(main_1_c1));  // open: dp
  Counter counter_2 (
    .load(rom_2_data[15]), .D({3'b000, controlled_buffer_2_out}), .count(rom_2_data[16]), .Q(counter_2_q),
    .clk(clock_1_out));  // open: carry, clr
  assign controlled_buffer_1_out = rom_2_data[17] ? counter_2_q : 8'bz;  // Controlled_Buffer controlled_buffer_1
  Register #(.width(16)) register_1 (
    .D(rom_1_data), .en(rom_2_data[14]), .Q({register_1_q[15:10], register_1_q_2, register_1_q[4:0]}),
    .clk(clock_1_out));  // open: clr
  LED led_9 (.in(decoder_1_out7));
  assign controlled_buffer_2_out = rom_2_data[13] ? register_1_q_2 : 5'bz;  // Controlled_Buffer controlled_buffer_2
  ROM #(.addrWidth(9), .dataWidth(19)) rom_2 (
    .addr({register_1_q[13:10], counter_1_q, register_6_q}), .data(rom_2_data));  // open: sel
  assign controlled_buffer_3_out = rom_2_data[12] ? register_1_q[4:0] : 5'bz;  // Controlled_Buffer controlled_buffer_3
  assign controlled_buffer_2_out = rom_2_data[11] ? register_1_q[4:0] : 5'bz;  // Controlled_Buffer controlled_buffer_4
  registersgpr_main main_2 (
    .Regout(rom_2_data[10]), .Regin(rom_2_data[9]), .Clk(clock_1_out), .Address_in(controlled_buffer_2_out),
    .Data_in(controlled_buffer_3_out[3:0]), .Data_Out(controlled_buffer_3_out[3:0]));  // open: reset
  // ram_main main_3: pin names not known; wires that end beside it: controlled_buffer_2_out, controlled_buffer_3_out[3:0], rom_2_data[9], clock_1_out, rom_2_data[10], controlled_buffer_3_out[3:0]
  Register #(.width(4)) register_2 (
    .D(controlled_buffer_3_out[3:0]), .en(rom_2_data[8]), .Q(register_2_q), .clk(clock_1_out));  // open: clr
  // alufinal_main main_4: pin names not known; wires that end beside it: rom_2_data[3], register_2_q, main_4_p3, main_4_p4, main_4_p5[0], main_4_p5[1]
  Register #(.width(4)) register_3 (
    .D(controlled_buffer_3_out[3:0]), .en(rom_2_data[6]), .Q(main_4_p3), .clk(clock_1_out));  // open: clr
  assign controlled_buffer_3_out[3:0] = rom_2_data[0] ? register_4_q : 4'bz;  // Controlled_Buffer controlled_buffer_5
  Register #(.width(4)) register_4 (
    .D(controlled_buffer_3_out[3:0]), .en(rom_2_data[1]), .Q(register_4_q), .clk(clock_1_out));  // open: clr
  assign controlled_buffer_3_out[3:0] = rom_2_data[7] ? register_2_q : 4'bz;  // Controlled_Buffer controlled_buffer_6
  assign controlled_buffer_3_out[3:0] = rom_2_data[5] ? main_4_p4 : 4'bz;  // Controlled_Buffer controlled_buffer_7
  assign controlled_buffer_3_out[3:0] = 1'b0 ? main_4_p3 : 4'bz;  // Controlled_Buffer controlled_buffer_8
  Register #(.width(4)) register_5 (
    .D(controlled_buffer_3_out[3:0]), .en(rom_2_data[18]), .Q(register_5_q), .clk(clock_1_out), .clr(undriven));
  Register #(.width(2)) register_6 (
    .D(main_4_p5), .en(rom_2_data[4]), .Q(register_6_q), .clk(clock_1_out));  // open: clr

  // Notes on the sheet:
  //   Flash ROM
  //   insert counter for CLU
  //   contents of rom_1 (hex, n*v repeats v):
  //   1466 9e3 4cf 1481 cc4 28c0 1ca0
  //   CE
  //   Instruction Register
  //   I in
  //   JMP
  //   Program Counter
  //   OI
  //   CE
  //   CO
  //   2
  //   0
  //   1
  //   ADRESS FROM JUMP INSTRUCTION
  //   ISHAO
  //   I(in)
  //   J
  //   5
  //   4
  //   3
  //   ISLAO
  //   ISLDO
  //   6
  //   CO
  //    DSO
  //   DSI
  //   9
  //   8
  //   7
  //   A(in)
  //   Aout
  //   Bin
  //   10
  //   11
  //   12
  //   SUB
  //   Eout
  //   FI
  //   13
  //   14
  //   T out
  //   T in
  //   MICR
  //   16
  //   17
  //   15
  //   18
  //   ISHAO
  //   contents of rom_2 (hex, n*v repeats v):
  //   4*24000 4*10000 24*0 4*24000 4*10000 4*c02 4*2201 4*4 12*0 4*24000 4*10000 4*c02 4*2201 4*4 12*0
  //   4*24000 4*10000 4*2500 4*c40 4*2220 4*4 8*0 4*24000 4*10000 4*2500 4*c40 4*2228 4*4 8*0 4*24000
  //   4*10000 4*3200 4*4 16*0 4*24000 4*10000 4*c02 4*2201 4*4 12*0 4*24000 4*10000 4*a000 4*4 16*0
  //   4*24000 4*10000 4 4 a000 a000 0 0 4 4 16*0 4*24000 4*10000 4 a000 4 a000 0 4 0 4 16*0 4*24000
  //   4*10000 4*42400 4*4
  //   Data Bus
  //   ISLDO
  //   ISLAO
  //   Address Bus
  //   GPR
  //   SRAM
  //   A in
  //   B in
  //   T in
  //   A reg
  //   B reg
  //   DSO
  //   DSI
  //   T out
  //   A out
  //   E out
  //   B out
  //   flag in
  //   SUB
endmodule
