// Logisim project REGISTER.circ as structural Verilog: 3 circuits, main circuit main
module main (
);

  REGISTER_MEMORY_LOADING register_memory_loading_1 ();  // open: P0, D0, P1, D1, P2, D2, P3, D3, P4, P5, P6, P7, ENABLE_FOR_MULTIPLICATION, E_FOR_MOVING, ADDRESS, E_FOR_READING, A0, A1, A2, D0_2, D1_2, D2_2, D3_2
endmodule

module PARLLEL_LOADING_TO_REGISTER (
  input  CONTROL,
  input  D0,
  input  D1,
  input  D2,
  input  D3,
  output R0,
  output R1,
  output R2,
  output R3
);

  D_Flip_Flop #(.trigger("high")) d_ff_1 (.clk(CONTROL), .D(D0), .Q(R0));  // open: Qn, preset, en, reset
  D_Flip_Flop #(.trigger("high")) d_ff_2 (.clk(CONTROL), .D(D1), .Q(R1));  // open: Qn, preset, en, reset
  D_Flip_Flop #(.trigger("high")) d_ff_3 (.clk(CONTROL), .D(D2), .Q(R2));  // open: Qn, preset, en, reset
  D_Flip_Flop #(.trigger("high")) d_ff_4 (.clk(CONTROL), .D(D3), .Q(R3));  // open: Qn, preset, en, reset
endmodule

module REGISTER_MEMORY_LOADING (
  input  P0,
  input  D0,
  input  P1,
  input  D1,
  input  P2,
  input  D2,
  input  P3,
  input  D3,
  input  P4,
  input  P5,
  input  P6,
  input  P7,
  input  ENABLE_FOR_MULTIPLICATION,
  input  E_FOR_MOVING,
  input  [2:0] ADDRESS,
  input  E_FOR_READING,
  input  A0,
  input  A1,
  input  A2,
  output D0_2,
  output D1_2,
  output D2_2,
  output D3_2
);

  wire controlled_buffer_1_out, controlled_buffer_2_out, controlled_buffer_3_out, controlled_buffer_4_out,
       controlled_buffer_5_out, controlled_buffer_6_out, controlled_buffer_7_out, controlled_buffer_8_out,
       controlled_buffer_9_out, controlled_buffer_10_out, controlled_buffer_11_out, controlled_buffer_12_out,
       controlled_buffer_13_out, controlled_buffer_14_out, controlled_buffer_15_out,
       controlled_buffer_16_out, decoder_1_out0, decoder_1_out1, decoder_1_out2, decoder_1_out3,
       decoder_1_out4, decoder_1_out5, decoder_1_out6, decoder_1_out7, or_1_out, or_3_out, or_4_out,
       or_6_out, or_7_out, or_8_out, or_9_out;
  wire [3:0] parllel_loading_to_register_1_r0, parllel_loading_to_register_2_r0,
       parllel_loading_to_register_3_r0, parllel_loading_to_register_5_r0, parllel_loading_to_register_6_r0,
       parllel_loading_to_register_7_r0, parllel_loading_to_register_8_r0;
  wire [3:1] parllel_loading_to_register_4_r0;

  assign controlled_buffer_1_out = ENABLE_FOR_MULTIPLICATION ? P0 : 1'bz;  // Controlled_Buffer controlled_buffer_1
  assign controlled_buffer_2_out = ENABLE_FOR_MULTIPLICATION ? P1 : 1'bz;  // Controlled_Buffer controlled_buffer_2
  assign controlled_buffer_3_out = ENABLE_FOR_MULTIPLICATION ? P2 : 1'bz;  // Controlled_Buffer controlled_buffer_3
  assign controlled_buffer_4_out = ENABLE_FOR_MULTIPLICATION ? P3 : 1'bz;  // Controlled_Buffer controlled_buffer_4
  assign controlled_buffer_5_out = ENABLE_FOR_MULTIPLICATION ? P4 : 1'bz;  // Controlled_Buffer controlled_buffer_5
  assign controlled_buffer_6_out = ENABLE_FOR_MULTIPLICATION ? P5 : 1'bz;  // Controlled_Buffer controlled_buffer_6
  assign controlled_buffer_7_out = ENABLE_FOR_MULTIPLICATION ? P6 : 1'bz;  // Controlled_Buffer controlled_buffer_7
  assign controlled_buffer_8_out = ENABLE_FOR_MULTIPLICATION ? P7 : 1'bz;  // Controlled_Buffer controlled_buffer_8
  Decoder #(.select(3)) decoder_1 (
    .out0(decoder_1_out0), .out1(decoder_1_out1), .out2(decoder_1_out2), .out3(decoder_1_out3),
    .out4(decoder_1_out4), .out5(decoder_1_out5), .out6(decoder_1_out6), .out7(decoder_1_out7),
    .sel({A2, A1, A0}), .en(E_FOR_MOVING));
  assign controlled_buffer_9_out = decoder_1_out0 ? D0 : 1'bz;  // Controlled_Buffer controlled_buffer_9
  assign controlled_buffer_10_out = decoder_1_out0 ? D1 : 1'bz;  // Controlled_Buffer controlled_buffer_10
  assign controlled_buffer_11_out = decoder_1_out0 ? D2 : 1'bz;  // Controlled_Buffer controlled_buffer_11
  assign controlled_buffer_12_out = decoder_1_out0 ? D3 : 1'bz;  // Controlled_Buffer controlled_buffer_12
  assign controlled_buffer_13_out = decoder_1_out1 ? D0 : 1'bz;  // Controlled_Buffer controlled_buffer_13
  assign controlled_buffer_14_out = decoder_1_out1 ? D1 : 1'bz;  // Controlled_Buffer controlled_buffer_14
  assign controlled_buffer_15_out = decoder_1_out1 ? D2 : 1'bz;  // Controlled_Buffer controlled_buffer_15
  assign controlled_buffer_16_out = decoder_1_out1 ? D3 : 1'bz;  // Controlled_Buffer controlled_buffer_16
  PARLLEL_LOADING_TO_REGISTER parllel_loading_to_register_1 (
    .CONTROL(decoder_1_out2), .D0(D0), .D1(D1), .D2(D2), .D3(D3), .R0(parllel_loading_to_register_1_r0[0]),
    .R1(parllel_loading_to_register_1_r0[1]), .R2(parllel_loading_to_register_1_r0[2]),
    .R3(parllel_loading_to_register_1_r0[3]));
  PARLLEL_LOADING_TO_REGISTER parllel_loading_to_register_2 (
    .CONTROL(decoder_1_out3), .D0(D0), .D1(D1), .D2(D2), .D3(D3), .R0(parllel_loading_to_register_2_r0[0]),
    .R1(parllel_loading_to_register_2_r0[1]), .R2(parllel_loading_to_register_2_r0[2]),
    .R3(parllel_loading_to_register_2_r0[3]));
  PARLLEL_LOADING_TO_REGISTER parllel_loading_to_register_3 (
    .CONTROL(decoder_1_out4), .D0(D0), .D1(D1), .D2(D2), .D3(D3), .R0(parllel_loading_to_register_3_r0[0]),
    .R1(parllel_loading_to_register_3_r0[1]), .R2(parllel_loading_to_register_3_r0[2]),
    .R3(parllel_loading_to_register_3_r0[3]));
  PARLLEL_LOADING_TO_REGISTER parllel_loading_to_register_4 (
    .CONTROL(decoder_1_out5), .D0(D0), .D1(D1), .D2(D2), .D3(D3), .R0(parllel_loading_to_register_4_r0[1]),
    .R1(parllel_loading_to_register_4_r0[1]), .R2(parllel_loading_to_register_4_r0[3]),
    .R3(parllel_loading_to_register_4_r0[3]));
  PARLLEL_LOADING_TO_REGISTER parllel_loading_to_register_5 (
    .CONTROL(decoder_1_out6), .D0(D0), .D1(D1), .D2(D2), .D3(D3), .R0(parllel_loading_to_register_5_r0[0]),
    .R1(parllel_loading_to_register_5_r0[1]), .R2(parllel_loading_to_register_5_r0[2]),
    .R3(parllel_loading_to_register_5_r0[3]));
  PARLLEL_LOADING_TO_REGISTER parllel_loading_to_register_6 (
    .CONTROL(decoder_1_out7), .D0(D0), .D1(D1), .D2(D2), .D3(D3), .R0(parllel_loading_to_register_6_r0[0]),
    .R1(parllel_loading_to_register_6_r0[1]), .R2(parllel_loading_to_register_6_r0[2]),
    .R3(parllel_loading_to_register_6_r0[3]));
  or or_1 (or_1_out, controlled_buffer_1_out, controlled_buffer_9_out);
  buf or_2 (ENABLE_FOR_MULTIPLICATION, decoder_1_out0);  // OR_Gate
  or or_3 (or_3_out, controlled_buffer_2_out, controlled_buffer_10_out);
  or or_4 (or_4_out, controlled_buffer_3_out, controlled_buffer_11_out);
  buf or_5 (ENABLE_FOR_MULTIPLICATION, decoder_1_out1);  // OR_Gate
  or or_6 (or_6_out, controlled_buffer_12_out, controlled_buffer_4_out);
  or or_7 (or_7_out, controlled_buffer_5_out, controlled_buffer_13_out);
  or or_8 (or_8_out, controlled_buffer_6_out, controlled_buffer_14_out);
  or or_9 (or_9_out, controlled_buffer_7_out, controlled_buffer_15_out);
  PARLLEL_LOADING_TO_REGISTER parllel_loading_to_register_7 (
    .CONTROL(ENABLE_FOR_MULTIPLICATION), .D0(or_1_out), .D1(or_3_out), .D2(or_4_out), .D3(or_6_out),
    .R0(parllel_loading_to_register_7_r0[0]), .R1(parllel_loading_to_register_7_r0[1]),
    .R2(parllel_loading_to_register_7_r0[2]), .R3(parllel_loading_to_register_7_r0[3]));
  PARLLEL_LOADING_TO_REGISTER parllel_loading_to_register_8 (
    .CONTROL(ENABLE_FOR_MULTIPLICATION), .D0(or_7_out), .D1(or_8_out), .D2(or_9_out),
    .D3(controlled_buffer_16_out), .R0(parllel_loading_to_register_8_r0[0]),
    .R1(parllel_loading_to_register_8_r0[1]), .R2(parllel_loading_to_register_8_r0[2]),
    .R3(parllel_loading_to_register_8_r0[3]));
  Multiplexer #(.select(3), .width(4)) multiplexer_1 (
    .in0(parllel_loading_to_register_7_r0), .in1(parllel_loading_to_register_8_r0),
    .in2(parllel_loading_to_register_1_r0), .in3(parllel_loading_to_register_2_r0),
    .in4(parllel_loading_to_register_3_r0),
    .in5({{2{parllel_loading_to_register_4_r0[3]}}, {2{parllel_loading_to_register_4_r0[1]}}}),
    .in6(parllel_loading_to_register_5_r0), .in7(parllel_loading_to_register_6_r0),
    .out({D3_2, D2_2, D1_2, D0_2}), .sel({A2, A1, A0}), .en(E_FOR_READING));
endmodule
