// Logisim project Sketch2.circ as structural Verilog: 1 circuit, main circuit main
module main (
  input  in_1,
  input  [7:0] in_2,
  input  Data_out,
  input  chip_select,
  input  [3:0] Programming_mode,
  input  in_6,
  input  in_7,
  input  in_8,
  input  B_out
);

  wire button_1_out, clock_1_out, comparator_1_eq, comparator_1_gt, comparator_1_lt, controlled_buffer_2_out,
       decoder_1_out0, decoder_1_out1, decoder_1_out2, decoder_1_out3, decoder_1_out4, decoder_1_out5,
       decoder_1_out6, decoder_1_out7, not_1_out, not_2_out;
  wire [1:0] nor_1_out, register_6_q;
  wire [3:0] controlled_buffer_1_out, controlled_buffer_4_out, counter_2_q, register_1_q;
  wire [4:2] counter_1_q;
  wire [7:0] adder_1_out, ram_1_data, register_2_q, register_3_q, register_4_q, register_5_q;
  wire [7:4] controlled_buffer_4_out_2;
  wire [14:0] rom_1_data;

  Clock clock_1 (.out(clock_1_out));
  Register #(.width(4)) register_1 (
    .D(controlled_buffer_4_out), .en(rom_1_data[14]), .Q(register_1_q), .clk(clock_1_out));  // open: clr
  assign controlled_buffer_1_out = not_2_out ? register_1_q : 4'bz;  // Controlled_Buffer controlled_buffer_1
  Register register_2 (
    .D({controlled_buffer_4_out_2, controlled_buffer_4_out}), .en(rom_1_data[10]), .Q(register_2_q),
    .clk(clock_1_out));  // open: clr
  not not_1 (not_1_out, clock_1_out);
  LED led_1 (.in(not_1_out));
  LED led_2 (.in(decoder_1_out0));
  assign controlled_buffer_2_out = not_2_out ? clock_1_out : 1'bz;  // Controlled_Buffer controlled_buffer_2
  assign controlled_buffer_1_out = in_6 ? Programming_mode : 4'bz;  // Controlled_Buffer controlled_buffer_3
  assign {controlled_buffer_4_out_2, controlled_buffer_4_out} = rom_1_data[11] ? register_2_q : 8'bz;  // Controlled_Buffer controlled_buffer_4
  // Probe on {register_2_q[7:4], counter_1_q, register_6_q}
  Counter #(.width(3), .max('h7)) counter_1 (
    .count(in_7), .Q(counter_1_q), .clk(not_1_out), .clr(decoder_1_out7));  // open: load, D, carry
  Decoder #(.select(3)) decoder_1 (
    .out0(decoder_1_out0), .out1(decoder_1_out1), .out2(decoder_1_out2), .out3(decoder_1_out3),
    .out4(decoder_1_out4), .out5(decoder_1_out5), .out6(decoder_1_out6), .out7(decoder_1_out7),
    .sel(counter_1_q), .en(in_8));
  LED led_3 (.in(decoder_1_out2));
  LED led_4 (.in(decoder_1_out3));
  LED led_5 (.in(decoder_1_out4));
  LED led_6 (.in(decoder_1_out1));
  assign {controlled_buffer_4_out_2, controlled_buffer_4_out} = rom_1_data[12] ? ram_1_data : 8'bz;  // Controlled_Buffer controlled_buffer_5
  RAM #(.addrWidth(4), .bus("separate")) ram_1 (
    .addr(controlled_buffer_1_out), .din(in_2), .data(ram_1_data), .str(in_6), .sel(chip_select),
    .clk(controlled_buffer_2_out), .ld(Data_out));  // open: clr
  not not_2 (not_2_out, in_6);
  Button button_1 (.out(button_1_out));
  LED led_7 (.in(decoder_1_out5));
  LED led_8 (.in(decoder_1_out6));
  ROM #(.addrWidth(9), .dataWidth(15)) rom_1 (
    .addr({register_2_q[7:4], counter_1_q, register_6_q}), .data(rom_1_data));  // open: sel
  LED led_9 (.in(controlled_buffer_4_out_2[7]));
  assign controlled_buffer_2_out = in_6 ? button_1_out : 1'bz;  // Controlled_Buffer controlled_buffer_6
  LED led_10 (.in(controlled_buffer_4_out_2[4]));
  LED led_11 (.in(controlled_buffer_4_out[3]));
  LED led_12 (.in(controlled_buffer_4_out_2[5]));
  LED led_13 (.in(controlled_buffer_4_out_2[6]));
  LED led_14 (.in(controlled_buffer_4_out[0]));
  LED led_15 (.in(controlled_buffer_4_out[1]));
  LED led_16 (.in(controlled_buffer_4_out[2]));
  LED led_17 (.in(rom_1_data[13]));
  Counter #(.width(4), .max('hf)) counter_2 (
    .load(rom_1_data[1]), .D(controlled_buffer_4_out), .count(rom_1_data[3]), .Q(counter_2_q),
    .clk(clock_1_out), .clr(in_1));  // open: carry
  assign {controlled_buffer_4_out_2, controlled_buffer_4_out} = rom_1_data[8] ? register_3_q : 8'bz;  // Controlled_Buffer controlled_buffer_7
  Register register_3 (
    .D({controlled_buffer_4_out_2, controlled_buffer_4_out}), .en(rom_1_data[9]), .Q(register_3_q),
    .clk(clock_1_out));  // open: clr
  Adder adder_1 (.a(register_3_q), .b(register_4_q), .out(adder_1_out), .cout(nor_1_out[1]));  // open: cin
  Comparator comparator_1 (
    .a(register_3_q), .b(register_4_q), .gt(comparator_1_gt), .eq(comparator_1_eq), .lt(comparator_1_lt));
  Register register_4 (
    .D({controlled_buffer_4_out_2, controlled_buffer_4_out}), .en(rom_1_data[5]), .Q(register_4_q),
    .clk(clock_1_out));  // open: clr
  assign {controlled_buffer_4_out_2, controlled_buffer_4_out} = B_out ? register_4_q : 8'bz;  // Controlled_Buffer controlled_buffer_8
  assign controlled_buffer_4_out = rom_1_data[2] ? counter_2_q : 4'bz;  // Controlled_Buffer controlled_buffer_9
  assign {controlled_buffer_4_out_2, controlled_buffer_4_out} = rom_1_data[7] ? adder_1_out : 8'bz;  // Controlled_Buffer controlled_buffer_10
  LED led_18 (.in(nor_1_out[1]));
  LED led_19 (.in(comparator_1_gt));
  LED led_20 (.in(comparator_1_eq));
  LED led_21 (.in(comparator_1_lt));
  Register register_5 (
    .D({controlled_buffer_4_out_2, controlled_buffer_4_out}), .en(rom_1_data[4]), .Q(register_5_q),
    .clk(clock_1_out));  // open: clr
  LED led_22 (.in(nor_1_out[0]));
  LED led_23 (.in(rom_1_data[6]));
  nor nor_1 (nor_1_out[0], adder_1_out[0], adder_1_out[1], adder_1_out[2], adder_1_out[3], adder_1_out[4], adder_1_out[5], adder_1_out[6], adder_1_out[7]);
  LED led_24 (.in(register_5_q[6]));
  LED led_25 (.in(register_5_q[4]));
  LED led_26 (.in(register_5_q[7]));
  LED led_27 (.in(register_5_q[5]));
  LED led_28 (.in(register_5_q[1]));
  LED led_29 (.in(register_5_q[2]));
  LED led_30 (.in(register_5_q[3]));
  LED led_31 (.in(register_5_q[0]));
  Register #(.width(2)) register_6 (
    .D(nor_1_out), .en(rom_1_data[0]), .Q(register_6_q), .clk(clock_1_out));  // open: clr

  // Notes on the sheet:
  //   RAM
  //   Memory Address Register 
  //   Instruction Register
  //   RAM
  //   Control Unit
  //   Inverted Clock
  //   Micro-instruction counter
  //   last 4 bits opcode and first 4 bits value or maybe not????
  //   contents of rom_1 (hex, n*v repeats v):
  //   4*4004 4*1408 24*0 4*4004 4*1408 4*4800 4*1200 16*0 4*4004 4*1408 4*4800 4*1020 4*281 12*0 4*4004
  //   4*1408 24*0 4*4004 4*1408 24*0 4*4004 4*1408 4*a00 20*0 4*4004 4*1408 4*802 20*0 4*4004 4*1408 0 0
  //   802 802 20*0 4*4004 4*1408 0 802 0 802 180*0 4*4004 4*1408 4*110 20*0 4*4004 4*1408
  //   **M in
  //   ALU
  //   B Register
  //   RI
  //   **R out
  //   Counter
  //   A Register
  //   **I out
  //   **I in
  //   Control Word
  //   carry out
  //   A>B
  //   A=B
  //   A<B
  //   **A in
  //   **A out
  //   E out**
  //   sub?
  //   **B in
  //   sum zero
  //   OI
  //    **CE
  //   **CO 
  //   Flags Register
  //   J 
  //   FI
endmodule
