// Logisim project alufinal.circ as structural Verilog: 1 circuit, main circuit main
// V flag
module main (
  input  Add_or_sub,
  input  [3:0] B_input,
  input  [3:0] A_input,
  output [3:0] Alu_Output
);

  wire adder_1_cout, and_1_out, and_2_out, nor_1_out, not_1_out, not_2_out, not_3_out, or_1_out, xor_5_out;
  wire [3:0] xor_1_out;

  xor xor_1 (xor_1_out[0], B_input[0], Add_or_sub);
  xor xor_2 (xor_1_out[1], B_input[1], Add_or_sub);
  xor xor_3 (xor_1_out[2], B_input[2], Add_or_sub);
  xor xor_4 (xor_1_out[3], B_input[3], Add_or_sub);
  Adder #(.width(4)) adder_1 (.a(xor_1_out), .b(A_input), .out(Alu_Output), .cin(Add_or_sub), .cout(adder_1_cout));
  not not_1 (not_1_out, Alu_Output[3]);
  not not_2 (not_2_out, B_input[3]);
  not not_3 (not_3_out, A_input[3]);
  and and_1 (and_1_out, B_input[3], A_input[3], not_1_out);
  and and_2 (and_2_out, Alu_Output[3], not_2_out, not_3_out);
  xor xor_5 (xor_5_out, Alu_Output[3], or_1_out);
  or or_1 (or_1_out, and_1_out, and_2_out);
  nor nor_1 (nor_1_out, Alu_Output[0], Alu_Output[1], Alu_Output[2], Alu_Output[3]);
  // Probe on nor_1_out
  // Probe on Alu_Output[3]
  // Probe on adder_1_cout
  // Probe on xor_5_out
  // Probe on or_1_out
endmodule
