// Logisim project registercircuit.circ as structural Verilog: 1 circuit, main circuit main
module main (
);

  wire and_1_out, and_2_out, and_3_out, and_4_out, and_5_out, and_6_out, and_7_out, and_8_out, and_9_out,
       and_10_out, and_11_out, and_12_out, and_13_out, and_14_out, and_15_out, and_16_out, decoder_1_out0,
       decoder_1_out1, decoder_1_out2, decoder_1_out3, decoder_1_out4, decoder_1_out5, decoder_1_out6,
       decoder_1_out7, undriven_2, undriven_4, undriven_5, undriven_6, undriven_7;
  wire [2:0] undriven_3;
  wire [3:0] controlled_buffer_1_out, register_1_q, register_2_q, register_3_q, register_4_q, register_5_q,
       register_6_q, register_7_q, register_8_q, undriven;

  Decoder #(.select(3)) decoder_1 (
    .out0(decoder_1_out0), .out1(decoder_1_out1), .out2(decoder_1_out2), .out3(decoder_1_out3),
    .out4(decoder_1_out4), .out5(decoder_1_out5), .out6(decoder_1_out6), .out7(decoder_1_out7),
    .sel(undriven_3), .en(undriven_2));
  and and_1 (and_1_out, undriven_4, decoder_1_out0);
  and and_2 (and_2_out, decoder_1_out0, undriven_5);
  and and_3 (and_3_out, undriven_4, decoder_1_out2);
  and and_4 (and_4_out, decoder_1_out2, undriven_5);
  and and_5 (and_5_out, undriven_4, decoder_1_out4);
  and and_6 (and_6_out, decoder_1_out4, undriven_5);
  and and_7 (and_7_out, undriven_4, decoder_1_out6);
  and and_8 (and_8_out, decoder_1_out6, undriven_5);
  Register #(.width(4)) register_1 (.D(undriven), .en(and_1_out), .clk(undriven_6), .Q(register_1_q), .clr(undriven_7));
  Register #(.width(4)) register_2 (.D(undriven), .en(and_3_out), .clk(undriven_6), .Q(register_2_q), .clr(undriven_7));
  Register #(.width(4)) register_3 (.D(undriven), .en(and_5_out), .clk(undriven_6), .Q(register_3_q), .clr(undriven_7));
  Register #(.width(4)) register_4 (.D(undriven), .en(and_7_out), .clk(undriven_6), .Q(register_4_q), .clr(undriven_7));
  assign controlled_buffer_1_out = and_2_out ? register_1_q : 4'bz;  // Controlled_Buffer controlled_buffer_1
  assign controlled_buffer_1_out = and_4_out ? register_2_q : 4'bz;  // Controlled_Buffer controlled_buffer_2
  assign controlled_buffer_1_out = and_8_out ? register_4_q : 4'bz;  // Controlled_Buffer controlled_buffer_3
  assign controlled_buffer_1_out = and_6_out ? register_3_q : 4'bz;  // Controlled_Buffer controlled_buffer_4
  and and_9 (and_9_out, undriven_4, decoder_1_out1);
  and and_10 (and_10_out, decoder_1_out1, undriven_5);
  and and_11 (and_11_out, undriven_4, decoder_1_out3);
  and and_12 (and_12_out, decoder_1_out3, undriven_5);
  and and_13 (and_13_out, undriven_4, decoder_1_out5);
  and and_14 (and_14_out, decoder_1_out5, undriven_5);
  and and_15 (and_15_out, undriven_4, decoder_1_out7);
  and and_16 (and_16_out, decoder_1_out7, undriven_5);
  Register #(.width(4)) register_5 (.D(undriven), .en(and_9_out), .clk(undriven_6), .Q(register_5_q), .clr(undriven_7));
  Register #(.width(4)) register_6 (
    .D(undriven), .en(and_11_out), .clk(undriven_6), .Q(register_6_q), .clr(undriven_7));
  Register #(.width(4)) register_7 (
    .D(undriven), .en(and_13_out), .clk(undriven_6), .Q(register_7_q), .clr(undriven_7));
  Register #(.width(4)) register_8 (
    .D(undriven), .en(and_15_out), .clk(undriven_6), .Q(register_8_q), .clr(undriven_7));
  assign controlled_buffer_1_out = and_12_out ? register_6_q : 4'bz;  // Controlled_Buffer controlled_buffer_5
  assign controlled_buffer_1_out = and_10_out ? register_5_q : 4'bz;  // Controlled_Buffer controlled_buffer_6
  assign controlled_buffer_1_out = and_14_out ? register_7_q : 4'bz;  // Controlled_Buffer controlled_buffer_7
  assign controlled_buffer_1_out = and_16_out ? register_8_q : 4'bz;  // Controlled_Buffer controlled_buffer_8

  // Notes on the sheet:
  //   address
  //   data in
  //   data out
  //   register enable
  //   Rin
  //   Rout
  //   reset
  //   clk
endmodule
